// Logisim project LOGISIM-Project_Bueno-Perez.circ as structural Verilog: 7 circuits, main circuit clock and buttons
module true_main (
  input  Mode_Selector
);

  wire automatic_pause_1_out_7, automatic_pause_1_out_8, clock_and_buttons_1_clock_signal,
       clock_and_buttons_1_jk_flipflop, clock_and_buttons_1_out_16, clock_and_buttons_1_out_17,
       clock_and_buttons_1_pause_led, clock_and_buttons_1_reset_bit_selector, Clock_out,
       Decrement__Minutes_out, Decrement__Seconds_out, Increment__Minutes_out, Increment__Seconds_out,
       left_led_seconds_1_out_6, left_led_seconds_1_out_7, multiplexer_1_out, multiplexer_2_out,
       multiplexer_3_out, Pause_Button_out, Play_Button_out, Reset_Button_out, right_led_minutes_1_out_8,
       right_led_minutes_1_out_9, right_led_seconds_1_out_6, right_led_seconds_1_out_7;
  wire [3:0] left_led_minutes_1_out_5, left_led_seconds_1_out_5, right_led_minutes_1_out_7,
       right_led_seconds_1_out_5;
  wire [6:0] left_led_minutes_1_out_4, left_led_seconds_1_out_4, right_led_minutes_1_out_6,
       right_led_seconds_1_out_4;

  Clock Clock (.out(Clock_out));
  Button Play_Button (.out(Play_Button_out));
  Button Pause_Button (.out(Pause_Button_out));
  Button Reset_Button (.out(Reset_Button_out));
  Button Increment__Seconds (.out(Increment__Seconds_out));
  Button Decrement__Seconds (.out(Decrement__Seconds_out));
  Button Increment__Minutes (.out(Increment__Minutes_out));
  Button Decrement__Minutes (.out(Decrement__Minutes_out));
  clock_and_buttons clock_and_buttons_1 (
    .Mode_Selector(Mode_Selector), .Clock(Clock_out), .Play(Play_Button_out), .Pause(Pause_Button_out),
    .Reset(Reset_Button_out), .Increment__seconds(Increment__Seconds_out),
    .Decrement__seconds(Decrement__Seconds_out), .Increment__minutes(Increment__Minutes_out),
    .Decrement__minutes(Decrement__Minutes_out), .out_16(clock_and_buttons_1_out_16),
    .out_17(clock_and_buttons_1_out_17), .jk_flipflop(clock_and_buttons_1_jk_flipflop),
    .clock_signal(clock_and_buttons_1_clock_signal),
    .reset_bit_selector(clock_and_buttons_1_reset_bit_selector), .in_7(automatic_pause_1_out_8),
    .in_8(automatic_pause_1_out_7), .Pause_LED(clock_and_buttons_1_pause_led));
  LED Pause_LED (.in(clock_and_buttons_1_pause_led));
  Multiplexer multiplexer_1 (
    .in0(right_led_seconds_1_out_6), .in1(right_led_seconds_1_out_7), .out(multiplexer_1_out),
    .sel(clock_and_buttons_1_jk_flipflop));  // open: en
  Right_LED__Seconds right_led_seconds_1 (
    .Mode_Selector(clock_and_buttons_1_jk_flipflop), .Clock(clock_and_buttons_1_clock_signal),
    .reset_bit_selector(clock_and_buttons_1_reset_bit_selector), .out_6(right_led_seconds_1_out_6),
    .out_7(right_led_seconds_1_out_7), .out_4(right_led_seconds_1_out_4), .out_5(right_led_seconds_1_out_5));
  Left_LED__Seconds left_led_seconds_1 (
    .Mode_Selector(clock_and_buttons_1_jk_flipflop), .Clock(multiplexer_1_out),
    .reset_bit_selector(clock_and_buttons_1_reset_bit_selector), .out_6(left_led_seconds_1_out_6),
    .out_7(left_led_seconds_1_out_7), .out_4(left_led_seconds_1_out_4), .out_5(left_led_seconds_1_out_5));
  Multiplexer multiplexer_2 (
    .in0(left_led_seconds_1_out_6), .in1(left_led_seconds_1_out_7), .out(multiplexer_2_out),
    .sel(clock_and_buttons_1_jk_flipflop));  // open: en
  Right_LED__Minutes right_led_minutes_1 (
    .Mode_Selector(clock_and_buttons_1_jk_flipflop), .Increment_bit_selector(clock_and_buttons_1_out_16),
    .Decrement_bit_selector(clock_and_buttons_1_out_17),
    .reset_bit_selector(clock_and_buttons_1_reset_bit_selector), .Clock(multiplexer_2_out),
    .out_8(right_led_minutes_1_out_8), .out_9(right_led_minutes_1_out_9), .out_6(right_led_minutes_1_out_6),
    .out_7(right_led_minutes_1_out_7));
  Multiplexer multiplexer_3 (
    .in0(right_led_minutes_1_out_8), .in1(right_led_minutes_1_out_9), .out(multiplexer_3_out),
    .sel(clock_and_buttons_1_jk_flipflop));  // open: en
  Left_LED__Minutes left_led_minutes_1 (
    .Mode_Selector(clock_and_buttons_1_jk_flipflop), .Clock(multiplexer_3_out),
    .reset_bit_selector(clock_and_buttons_1_reset_bit_selector), .out_4(left_led_minutes_1_out_4),
    .out_5(left_led_minutes_1_out_5));
  Automatic_Pause automatic_pause_1 (
    .Left_LED__seconds(right_led_seconds_1_out_5), .Mode_Selector(clock_and_buttons_1_jk_flipflop),
    .Right_LED__seconds(left_led_seconds_1_out_5), .Left_LED__minutes(right_led_minutes_1_out_7),
    .Mode_Selector_2(clock_and_buttons_1_jk_flipflop), .Right_LED__minutes(left_led_minutes_1_out_5),
    .out_7(automatic_pause_1_out_7), .out_8(automatic_pause_1_out_8));
  _7_Segment_Display u_7_segment_display_1 (
    .g(left_led_minutes_1_out_4[6]), .f(left_led_minutes_1_out_4[5]), .a(left_led_minutes_1_out_4[0]),
    .b(left_led_minutes_1_out_4[1]), .e(left_led_minutes_1_out_4[4]), .d(left_led_minutes_1_out_4[3]),
    .c(left_led_minutes_1_out_4[2]));  // open: dp
  _7_Segment_Display u_7_segment_display_2 (
    .g(right_led_minutes_1_out_6[6]), .f(right_led_minutes_1_out_6[5]), .a(right_led_minutes_1_out_6[0]),
    .b(right_led_minutes_1_out_6[1]), .e(right_led_minutes_1_out_6[4]), .d(right_led_minutes_1_out_6[3]),
    .c(right_led_minutes_1_out_6[2]));  // open: dp
  _7_Segment_Display u_7_segment_display_3 (
    .g(left_led_seconds_1_out_4[6]), .f(left_led_seconds_1_out_4[5]), .a(left_led_seconds_1_out_4[0]),
    .b(left_led_seconds_1_out_4[1]), .e(left_led_seconds_1_out_4[4]), .d(left_led_seconds_1_out_4[3]),
    .c(left_led_seconds_1_out_4[2]));  // open: dp
  _7_Segment_Display u_7_segment_display_4 (
    .g(right_led_seconds_1_out_4[6]), .f(right_led_seconds_1_out_4[5]), .a(right_led_seconds_1_out_4[0]),
    .b(right_led_seconds_1_out_4[1]), .e(right_led_seconds_1_out_4[4]), .d(right_led_seconds_1_out_4[3]),
    .c(right_led_seconds_1_out_4[2]));  // open: dp
endmodule

module clock_and_buttons (
  input  Mode_Selector,
  input  Clock,
  input  Play,
  input  Pause,
  input  Reset,
  input  Increment__seconds,
  input  in_7,
  input  in_8,
  input  Decrement__seconds,
  input  Increment__minutes,
  input  Decrement__minutes,
  output jk_flipflop,
  output clock_signal,
  output reset_bit_selector,
  output Pause_LED,
  output out_16,
  output out_17
);

  wire d_ff_1_q, multiplexer_1_out, multiplexer_2_out, multiplexer_3_out, multiplexer_5_out, not_1_out,
       or_1_out, or_2_out, transistor_1_out;

  Transistor #(.\type ("n"), .gate("br")) transistor_1 (.in(1'b0), .out(transistor_1_out), .gate(Pause_LED));
  Transistor #(.gate("br")) transistor_2 (.in(Clock), .out(transistor_1_out), .gate(Pause_LED));
  Multiplexer multiplexer_1 (.in0(Pause), .in1(1'b1), .out(multiplexer_1_out), .sel(Reset));  // open: en
  Transistor #(.gate("br")) transistor_3 (.in(Mode_Selector), .out(jk_flipflop), .gate(Pause_LED));
  Register #(.width(1)) register_1 (.D(1'b1), .Q(Pause_LED), .clk(multiplexer_2_out), .clr(Play));  // open: en
  Multiplexer multiplexer_2 (.in0(multiplexer_1_out), .in1(1'b1), .out(multiplexer_2_out), .sel(in_8));  // open: en
  or or_1 (or_1_out, Increment__seconds, Increment__minutes);
  or or_2 (or_2_out, Decrement__seconds, Decrement__minutes);
  not not_1 (not_1_out, Pause_LED);
  D_Flip_Flop d_ff_1 (.clk(1'b1), .D(1'b1), .Q(d_ff_1_q), .preset(or_2_out), .reset(or_1_out));  // open: Qn, en
  Multiplexer multiplexer_3 (
    .in0(transistor_1_out), .in1(1'b1), .out(multiplexer_3_out), .sel(Increment__seconds));  // open: en
  Multiplexer multiplexer_4 (
    .in0(multiplexer_3_out), .in1(1'b1), .out(clock_signal), .sel(multiplexer_5_out));  // open: en
  Multiplexer multiplexer_5 (.in0(Decrement__seconds), .in1(1'b0), .out(multiplexer_5_out), .sel(in_7));  // open: en
  Transistor #(.gate("br")) transistor_4 (.in(d_ff_1_q), .out(jk_flipflop), .gate(not_1_out));

  assign out_16 = Increment__minutes;
  assign out_17 = Decrement__minutes;
  assign reset_bit_selector = Reset;
endmodule

module Right_LED__Seconds (
  input  Mode_Selector,
  input  Clock,
  input  reset_bit_selector,
  output [6:0] out_4,
  output [3:0] out_5,
  output out_6,
  output out_7
);

  wire and_1_out, and_2_out, and_3_out, and_4_out, and_5_out, and_6_out, j_k_ff_1_qn, j_k_ff_2_qn,
       j_k_ff_3_qn, multiplexer_1_out, multiplexer_2_out, multiplexer_3_out, not_1_out, not_2_out, or_1_out,
       or_2_out, or_3_out;

  not not_1 (not_1_out, Mode_Selector);
  not not_2 (not_2_out, not_1_out);
  J_K_Flip_Flop #(.trigger("falling")) j_k_ff_1 (
    .J(1'b1), .clk(Clock), .K(1'b1), .Q(out_5[0]), .Qn(j_k_ff_1_qn), .reset(multiplexer_1_out));  // open: preset, en
  and and_1 (and_1_out, not_1_out, out_5[0]);
  and and_2 (and_2_out, j_k_ff_1_qn, not_2_out);
  or or_1 (or_1_out, and_1_out, and_2_out);
  J_K_Flip_Flop #(.trigger("falling")) j_k_ff_2 (
    .J(or_1_out), .clk(Clock), .K(or_1_out), .Q(out_5[1]), .Qn(j_k_ff_2_qn), .reset(multiplexer_2_out));  // open: preset, en
  and and_3 (and_3_out, and_1_out, out_5[1]);
  and and_4 (and_4_out, j_k_ff_2_qn, and_2_out);
  or or_2 (or_2_out, and_3_out, and_4_out);
  and and_5 (and_5_out, and_3_out, out_5[2]);
  J_K_Flip_Flop #(.trigger("falling")) j_k_ff_3 (
    .J(or_2_out), .clk(Clock), .K(or_2_out), .Q(out_5[2]), .Qn(j_k_ff_3_qn), .reset(multiplexer_2_out));  // open: preset, en
  and and_6 (and_6_out, j_k_ff_3_qn, and_4_out);
  or or_3 (or_3_out, and_5_out, and_6_out);
  J_K_Flip_Flop #(.trigger("falling")) j_k_ff_4 (
    .J(or_3_out), .clk(Clock), .K(or_3_out), .Q(out_5[3]), .reset(multiplexer_1_out));  // open: Qn, preset, en
  // _7_segment_display_driver 7_segment_display_driver_1: pin names not known; wires that end beside it: out_5[3], out_5[2], out_5[1], out_5[0], out_4[0], out_4[1], out_4[2], out_4[3], out_4[4], out_4[5], out_4[6]
  Comparator #(.width(4)) comparator_1 (.a(out_5), .b(4'b1010), .eq(out_6));  // open: gt, lt
  Multiplexer multiplexer_1 (.in0(out_6), .in1(1'b1), .out(multiplexer_1_out), .sel(reset_bit_selector));  // open: en
  Multiplexer multiplexer_2 (
    .in0(multiplexer_1_out), .in1(multiplexer_3_out), .out(multiplexer_2_out), .sel(Mode_Selector));  // open: en
  Comparator #(.width(4)) comparator_2 (.a(out_5), .b(4'b1111), .eq(out_7));  // open: gt, lt
  Multiplexer multiplexer_3 (.in0(out_7), .in1(1'b1), .out(multiplexer_3_out), .sel(reset_bit_selector));  // open: en
endmodule

module Left_LED__Seconds (
  input  Mode_Selector,
  input  Clock,
  input  reset_bit_selector,
  output [6:0] out_4,
  output [3:0] out_5,
  output out_6,
  output out_7
);

  wire and_1_out, and_2_out, and_3_out, and_4_out, and_5_out, and_6_out, j_k_ff_1_qn, j_k_ff_2_qn,
       j_k_ff_3_qn, multiplexer_1_out, multiplexer_2_out, multiplexer_3_out, not_1_out, not_2_out, or_1_out,
       or_2_out, or_3_out;

  not not_1 (not_1_out, Mode_Selector);
  not not_2 (not_2_out, not_1_out);
  J_K_Flip_Flop #(.trigger("falling")) j_k_ff_1 (
    .J(1'b1), .clk(Clock), .K(1'b1), .Q(out_5[0]), .Qn(j_k_ff_1_qn), .reset(multiplexer_1_out));  // open: preset, en
  and and_1 (and_1_out, not_1_out, out_5[0]);
  and and_2 (and_2_out, j_k_ff_1_qn, not_2_out);
  or or_1 (or_1_out, and_1_out, and_2_out);
  J_K_Flip_Flop #(.trigger("falling")) j_k_ff_2 (
    .J(or_1_out), .clk(Clock), .K(or_1_out), .Q(out_5[1]), .Qn(j_k_ff_2_qn), .reset(multiplexer_2_out));  // open: preset, en
  and and_3 (and_3_out, and_1_out, out_5[1]);
  and and_4 (and_4_out, j_k_ff_2_qn, and_2_out);
  or or_2 (or_2_out, and_3_out, and_4_out);
  and and_5 (and_5_out, and_3_out, out_5[2]);
  J_K_Flip_Flop #(.trigger("falling")) j_k_ff_3 (
    .J(or_2_out), .clk(Clock), .K(or_2_out), .Q(out_5[2]), .Qn(j_k_ff_3_qn), .reset(multiplexer_1_out));  // open: preset, en
  and and_6 (and_6_out, j_k_ff_3_qn, and_4_out);
  or or_3 (or_3_out, and_5_out, and_6_out);
  J_K_Flip_Flop #(.trigger("falling")) j_k_ff_4 (
    .J(or_3_out), .clk(Clock), .K(or_3_out), .Q(out_5[3]), .reset(multiplexer_2_out));  // open: Qn, preset, en
  // _7_segment_display_driver 7_segment_display_driver_1: pin names not known; wires that end beside it: out_5[3], out_5[2], out_5[1], out_5[0], out_4[0], out_4[1], out_4[2], out_4[3], out_4[4], out_4[5], out_4[6]
  Comparator #(.width(4)) comparator_1 (.a(out_5), .b(4'b0110), .eq(out_6));  // open: gt, lt
  Multiplexer multiplexer_1 (.in0(out_6), .in1(1'b1), .out(multiplexer_1_out), .sel(reset_bit_selector));  // open: en
  Multiplexer multiplexer_2 (
    .in0(multiplexer_1_out), .in1(multiplexer_3_out), .out(multiplexer_2_out), .sel(Mode_Selector));  // open: en
  Comparator #(.width(4)) comparator_2 (.a(out_5), .b(4'b1111), .eq(out_7));  // open: gt, lt
  Multiplexer multiplexer_3 (.in0(out_7), .in1(1'b1), .out(multiplexer_3_out), .sel(reset_bit_selector));  // open: en
endmodule

module Right_LED__Minutes (
  input  Clock,
  input  Mode_Selector,
  input  Increment_bit_selector,
  input  Decrement_bit_selector,
  input  reset_bit_selector,
  output [6:0] out_6,
  output [3:0] out_7,
  output out_8,
  output out_9
);

  wire and_1_out, and_2_out, and_3_out, and_4_out, and_5_out, and_6_out, j_k_ff_1_qn, j_k_ff_2_qn,
       j_k_ff_3_qn, multiplexer_1_out, multiplexer_2_out, multiplexer_3_out, multiplexer_4_out,
       multiplexer_5_out, not_1_out, not_2_out, or_1_out, or_2_out, or_3_out;

  Multiplexer multiplexer_1 (
    .in0(Clock), .in1(1'b1), .out(multiplexer_1_out), .sel(Increment_bit_selector));  // open: en
  Multiplexer multiplexer_2 (
    .in0(multiplexer_1_out), .in1(1'b1), .out(multiplexer_2_out), .sel(Decrement_bit_selector));  // open: en
  not not_1 (not_1_out, Mode_Selector);
  not not_2 (not_2_out, not_1_out);
  J_K_Flip_Flop #(.trigger("falling")) j_k_ff_1 (
    .J(1'b1), .clk(multiplexer_2_out), .K(1'b1), .Q(out_7[0]), .Qn(j_k_ff_1_qn), .reset(multiplexer_3_out));  // open: preset, en
  and and_1 (and_1_out, not_1_out, out_7[0]);
  and and_2 (and_2_out, j_k_ff_1_qn, not_2_out);
  or or_1 (or_1_out, and_1_out, and_2_out);
  and and_3 (and_3_out, and_1_out, out_7[1]);
  J_K_Flip_Flop #(.trigger("falling")) j_k_ff_2 (
    .J(or_1_out), .clk(multiplexer_2_out), .K(or_1_out), .Q(out_7[1]), .Qn(j_k_ff_2_qn),
    .reset(multiplexer_4_out));  // open: preset, en
  and and_4 (and_4_out, j_k_ff_2_qn, and_2_out);
  or or_2 (or_2_out, and_3_out, and_4_out);
  J_K_Flip_Flop #(.trigger("falling")) j_k_ff_3 (
    .J(or_2_out), .clk(multiplexer_2_out), .K(or_2_out), .Q(out_7[2]), .Qn(j_k_ff_3_qn),
    .reset(multiplexer_4_out));  // open: preset, en
  and and_5 (and_5_out, and_3_out, out_7[2]);
  and and_6 (and_6_out, j_k_ff_3_qn, and_4_out);
  or or_3 (or_3_out, and_5_out, and_6_out);
  J_K_Flip_Flop #(.trigger("falling")) j_k_ff_4 (
    .J(or_3_out), .clk(multiplexer_2_out), .K(or_3_out), .Q(out_7[3]), .reset(multiplexer_3_out));  // open: Qn, preset, en
  // _7_segment_display_driver 7_segment_display_driver_1: pin names not known; wires that end beside it: out_7[3], out_7[2], out_7[1], out_7[0], out_6[0], out_6[1], out_6[2], out_6[3], out_6[4], out_6[5], out_6[6]
  Comparator #(.width(4)) comparator_1 (.a(out_7), .b(4'b1010), .eq(out_8));  // open: gt, lt
  Multiplexer multiplexer_3 (.in0(out_8), .in1(1'b1), .out(multiplexer_3_out), .sel(reset_bit_selector));  // open: en
  Comparator #(.width(4)) comparator_2 (.a(out_7), .b(4'b1111), .eq(out_9));  // open: gt, lt
  Multiplexer multiplexer_4 (
    .in0(multiplexer_3_out), .in1(multiplexer_5_out), .out(multiplexer_4_out), .sel(Mode_Selector));  // open: en
  Multiplexer multiplexer_5 (.in0(out_9), .in1(1'b1), .out(multiplexer_5_out), .sel(reset_bit_selector));  // open: en
endmodule

module Left_LED__Minutes (
  input  Mode_Selector,
  input  Clock,
  input  reset_bit_selector,
  output [6:0] out_4,
  output [3:0] out_5
);

  wire and_1_out, and_2_out, and_3_out, and_4_out, and_5_out, and_6_out, comparator_1_eq, comparator_2_eq,
       j_k_ff_1_qn, j_k_ff_2_qn, j_k_ff_3_qn, multiplexer_1_out, multiplexer_2_out, multiplexer_3_out,
       not_1_out, not_2_out, or_1_out, or_2_out, or_3_out;

  not not_1 (not_1_out, Mode_Selector);
  not not_2 (not_2_out, not_1_out);
  J_K_Flip_Flop #(.trigger("falling")) j_k_ff_1 (
    .J(1'b1), .clk(Clock), .K(1'b1), .Q(out_5[0]), .Qn(j_k_ff_1_qn), .reset(multiplexer_1_out));  // open: preset, en
  and and_1 (and_1_out, not_1_out, out_5[0]);
  and and_2 (and_2_out, j_k_ff_1_qn, not_2_out);
  or or_1 (or_1_out, and_1_out, and_2_out);
  J_K_Flip_Flop #(.trigger("falling")) j_k_ff_2 (
    .J(or_1_out), .clk(Clock), .K(or_1_out), .Q(out_5[1]), .Qn(j_k_ff_2_qn), .reset(multiplexer_2_out));  // open: preset, en
  and and_3 (and_3_out, and_1_out, out_5[1]);
  and and_4 (and_4_out, j_k_ff_2_qn, and_2_out);
  or or_2 (or_2_out, and_3_out, and_4_out);
  and and_5 (and_5_out, and_3_out, out_5[2]);
  J_K_Flip_Flop #(.trigger("falling")) j_k_ff_3 (
    .J(or_2_out), .clk(Clock), .K(or_2_out), .Q(out_5[2]), .Qn(j_k_ff_3_qn), .reset(multiplexer_1_out));  // open: preset, en
  and and_6 (and_6_out, j_k_ff_3_qn, and_4_out);
  or or_3 (or_3_out, and_5_out, and_6_out);
  J_K_Flip_Flop #(.trigger("falling")) j_k_ff_4 (
    .J(or_3_out), .clk(Clock), .K(or_3_out), .Q(out_5[3]), .reset(multiplexer_2_out));  // open: Qn, preset, en
  // _7_segment_display_driver 7_segment_display_driver_1: pin names not known; wires that end beside it: out_5[3], out_5[2], out_5[1], out_5[0], out_4[0], out_4[1], out_4[2], out_4[3], out_4[4], out_4[5], out_4[6]
  Comparator #(.width(4)) comparator_1 (.a(out_5), .b(4'b0110), .eq(comparator_1_eq));  // open: gt, lt
  Multiplexer multiplexer_1 (
    .in0(comparator_1_eq), .in1(1'b1), .out(multiplexer_1_out), .sel(reset_bit_selector));  // open: en
  Multiplexer multiplexer_2 (
    .in0(multiplexer_1_out), .in1(multiplexer_3_out), .out(multiplexer_2_out), .sel(Mode_Selector));  // open: en
  Comparator #(.width(4)) comparator_2 (.a(out_5), .b(4'b1111), .eq(comparator_2_eq));  // open: gt, lt
  Multiplexer multiplexer_3 (
    .in0(comparator_2_eq), .in1(1'b1), .out(multiplexer_3_out), .sel(reset_bit_selector));  // open: en
endmodule

module Automatic_Pause (
  input  [3:0] Left_LED__seconds,
  input  Mode_Selector,
  input  [3:0] Right_LED__seconds,
  input  [3:0] Left_LED__minutes,
  input  Mode_Selector_2,
  input  [3:0] Right_LED__minutes,
  output out_7,
  output out_8
);

  wire and_1_out, and_3_out, and_4_out, comparator_1_eq, comparator_2_eq, comparator_3_eq, comparator_4_eq,
       comparator_5_eq, comparator_6_eq, comparator_7_eq, comparator_8_eq, not_1_out;

  Comparator #(.width(4)) comparator_1 (.a(Left_LED__seconds), .b(4'b1001), .eq(comparator_1_eq));  // open: gt, lt
  Comparator #(.width(4)) comparator_2 (.a(Left_LED__seconds), .b(4'b0000), .eq(comparator_2_eq));  // open: gt, lt
  Comparator #(.width(4)) comparator_3 (.a(Right_LED__seconds), .b(4'b0101), .eq(comparator_3_eq));  // open: gt, lt
  Comparator #(.width(4)) comparator_4 (.a(Right_LED__seconds), .b(4'b0000), .eq(comparator_4_eq));  // open: gt, lt
  Comparator #(.width(4)) comparator_5 (.a(Left_LED__minutes), .b(4'b1001), .eq(comparator_5_eq));  // open: gt, lt
  Comparator #(.width(4)) comparator_6 (.a(Left_LED__minutes), .b(4'b0000), .eq(comparator_6_eq));  // open: gt, lt
  Comparator #(.width(4)) comparator_7 (.a(Right_LED__minutes), .b(4'b0101), .eq(comparator_7_eq));  // open: gt, lt
  Comparator #(.width(4)) comparator_8 (.a(Right_LED__minutes), .b(4'b0000), .eq(comparator_8_eq));  // open: gt, lt
  and and_1 (and_1_out, comparator_1_eq, comparator_3_eq, comparator_5_eq, comparator_7_eq);
  and and_2 (out_8, comparator_2_eq, comparator_4_eq, comparator_6_eq, comparator_8_eq);
  and and_3 (and_3_out, and_1_out, not_1_out);
  not not_1 (not_1_out, Mode_Selector);
  and and_4 (and_4_out, out_8, Mode_Selector_2);
  or or_1 (out_7, and_3_out, and_4_out);
endmodule
